// Logisim project 8X1 multiplexer.circ as structural Verilog: 1 circuit, main circuit main
module main (
  input  D0,
  input  D1,
  input  D2,
  input  D3,
  input  D4,
  input  D5,
  input  D6,
  input  D7,
  input  S0,
  input  S1,
  input  S2,
  output Y_output
);

  wire not_1_out, not_2_out, not_3_out, Y0_out, Y1_out, Y2_out, Y3_out, Y4_out, Y5_out, Y6_out, Y7_out;

  not not_1 (not_1_out, S0);
  not not_2 (not_2_out, S1);
  not not_3 (not_3_out, S2);
  and Y0 (Y0_out, D0, not_1_out, not_2_out, not_3_out);
  and Y1 (Y1_out, D1, S2, not_2_out, not_1_out);
  and Y2 (Y2_out, D2, not_3_out, S1, not_1_out);
  and Y3 (Y3_out, D3, not_2_out, S2, not_1_out);
  and Y4 (Y4_out, D4, not_2_out, not_3_out, S0);
  and Y5 (Y5_out, D5, S2, not_2_out, S0);
  and Y6 (Y6_out, D6, not_3_out, S1, S0);
  and Y7 (Y7_out, D7, S0, S1, S2);
  or or_1 (Y_output, Y0_out, Y1_out, Y2_out, Y3_out, Y4_out, Y5_out, Y6_out, Y7_out);
endmodule
